# Fritzing sketch esquematico (saved by Fritzing 0.9.3b)
breadboards: 1

parts:
  Part1 = LC Studio SD Card Module
  Part2 = Arduino Mega 2560 (Rev3)
  R1 = Resistor [tolerance=±5% resistance=220 package="2010 [SMD]"]
  R7 = Resistor [tolerance=±5% resistance=220 package="2010 [SMD]"]
  R8 = Resistor [tolerance=±5% resistance=330 package="2010 [SMD]"]
  R9 = Resistor [tolerance=±5% resistance=330 package="2010 [SMD]"]
  R10 = Resistor [tolerance=±5% resistance=330 package="2010 [SMD]"]
  R11 = Resistor [tolerance=±5% resistance=220 package="2010 [SMD]"]
  ZS-042_RTC1 = ZS-042 RTC Module

nets:
  5V: Part1.5V, Part2.5V, ZS-042_RTC1.VCC
  N1: Part1.CS, R9.Pin_0, R11.Pin_1
  N2: Part1.MOSI, R1.Pin_1, R8.Pin_0
  N3: Part1.SCK, R7.Pin_1, R10.Pin_0
  N4: Part1.MISO, Part2.D13_PWM
  GND: Part1.GND, Part2.GND, R8.Pin_1, R9.Pin_1, R10.Pin_1, ZS-042_RTC1.GND
  N5: Part2.A4, ZS-042_RTC1.SDA
  N6: Part2.A5, ZS-042_RTC1.SCL
  N7: Part2.D12_PWM, R11.Pin_0
  N8: Part2.D11_PWM, R1.Pin_0
  N9: Part2.D10_PWM, R7.Pin_0

custom parts:
  LC Studio SD Card Module: The LC Studio SD card module serves as an interface to an SD card. The module works at 3.3 volts and 5 volts. The SPI (Serial Peripheral Interface) protocol is used for communicating with the module.
